# Fritzing sketch 170406 Bike_Blink_v0 (saved by Fritzing 0.9.2b)
breadboards: 1

parts:
  Part2 = Arduino Nano (Rev3.0) (ICSP)
  NEOPIXEL1 = Neopixel Strip -- Black (30/m)
  NEOPIXEL2 = Neopixel Strip -- Black (30/m)
  LED1 = LED - 5mm [color="Red (633nm)" package="5 mm [THT]"]
  R1 = Resistor [tolerance=±5% resistance=33 package=THT]

nets:
  GND: Part2.GND, NEOPIXEL1.GND, NEOPIXEL2.GND, R1.Pin_0
  N1: Part2.D7, NEOPIXEL2.Din
  N2: Part2.D8, NEOPIXEL1.Din
  N3: Part2.D12/MISO, LED1.anode
  +5V: Part2.5V, NEOPIXEL1.+5V, NEOPIXEL2.+5V
  N4: LED1.cathode, R1.Pin_1

notes:
  HG-208GD 315Mhz-433Mhz
  Vt V3 V2 V1 V0 5V GND

custom parts:
  Neopixel Strip -- Black (30/m): These NeoPixel strips have 30 digitally-addressable pixel LEDs per meter and are very affordable and are only 12.5 mm wide, 10 mm if you remove the strip from the casing.
